// Logisim project Lab1.circ as structural Verilog
module _2to1MUX (
  input  in_B,
  input  Slelect,
  input  in_A,
  output Out
);

  wire and_1_out, and_2_out, not_1_out;

  not not_1 (not_1_out, Slelect);
  and and_1 (and_1_out, in_B, Slelect);
  and and_2 (and_2_out, not_1_out, in_A);
  or or_1 (Out, and_1_out, and_2_out);
endmodule

module _8_1_Mux (
  input  input_0,
  input  input_1,
  input  Select_1,
  input  input_2,
  input  select_0,
  input  input_3,
  output out_7
);

  wire n2to1mux_1_out, n2to1mux_2_out;

  _2to1MUX u_2to1mux_1 (.in_B(input_0), .Slelect(select_0), .in_A(input_1), .Out(n2to1mux_1_out));
  _2to1MUX u_2to1mux_2 (.in_B(input_2), .Slelect(select_0), .in_A(input_3), .Out(n2to1mux_2_out));
  _2to1MUX u_2to1mux_3 (.in_B(n2to1mux_1_out), .Slelect(Select_1), .in_A(n2to1mux_2_out), .Out(out_7));
endmodule

module real_8_1 (
  input  in_0,
  input  Select_0,
  input  in_1,
  input  Select_1,
  input  in_2,
  input  in_3,
  input  Select_2,
  input  in_0_2,
  input  in_1_2,
  input  in_2_2,
  input  in_3_2,
  output out_12
);

  wire n8_1_mux_1_out_7, n8_1_mux_2_out_7;

  _8_1_Mux u_8_1_mux_1 (
    .input_0(in_0), .input_1(Select_0), .Select_1(in_1), .input_2(Select_1), .select_0(in_2), .input_3(in_3),
    .out_7(n8_1_mux_1_out_7));
  _8_1_Mux u_8_1_mux_2 (
    .input_0(in_0_2), .input_1(Select_0), .Select_1(in_1_2), .input_2(Select_1), .select_0(in_2_2),
    .input_3(in_3_2), .out_7(n8_1_mux_2_out_7));
  _2to1MUX u_2to1mux_1 (.in_B(n8_1_mux_1_out_7), .Slelect(Select_2), .in_A(n8_1_mux_2_out_7), .Out(out_12));
  _2to1MUX u_2to1mux_2 ();  // open: in_B, Slelect, in_A, Out
endmodule
